// Logisim project CAProject.circ as structural Verilog: 4 circuits, main circuit ALSU
module ALSU (
  input  cin,
  input  [3:0] A,
  input  _0,
  input  s3,
  input  s2,
  input  [3:0] B,
  input  [1:0] s1__s0,
  input  SIR,
  input  SIL,
  output [3:0] F,
  output cout
);

  wire [3:0] au_1_y, lu_1_y, shift_1_f;

  shift shift_1 (.Serial_input_L(SIR), .A(A), .RSerial_input_R(SIL), .S(s2), .F(shift_1_f));
  AU au_1 (.cin(cin), .A(A), .B(B), ._0(_0), .s(s1__s0), .cout(cout), .Y(au_1_y));
  LU lu_1 (.A(A), .B(B), .s(s1__s0), .Y(lu_1_y));
  Multiplexer #(.select(2), .width(4), .disabled(0), .enable("false")) multiplexer_1 (
    .in0(au_1_y), .in1(lu_1_y), .in2(shift_1_f), .in3(shift_1_f), .out(F), .sel({s3, s2}));
endmodule

module LU (
  input  [3:0] A,
  input  [3:0] B,
  input  [1:0] s,
  output [3:0] Y
);

  wire [3:0] and_1_out, not_1_out, or_1_out, xor_1_out;

  assign and_1_out = A & B;  // AND_Gate and_1, 4 bits wide
  assign or_1_out = A | B;  // OR_Gate or_1, 4 bits wide
  assign xor_1_out = A ^ B;  // XOR_Gate xor_1, 4 bits wide
  assign not_1_out = ~A;  // NOT_Gate not_1, 4 bits wide
  Multiplexer #(.select(2), .width(4), .disabled(0), .enable("false")) multiplexer_1 (
    .in0(and_1_out), .in1(or_1_out), .in2(xor_1_out), .in3(not_1_out), .out(Y), .sel(s));
endmodule

// Shift
module shift (
  input  Serial_input_L,
  input  [3:0] A,
  input  RSerial_input_R,
  input  S,
  output [3:0] F
);

  Multiplexer #(.disabled(0), .enable("false")) multiplexer_1 (.in0(Serial_input_L), .in1(A[1]), .out(F[0]), .sel(S));
  Multiplexer #(.disabled(0), .enable("false")) multiplexer_2 (.in0(A[0]), .in1(A[2]), .out(F[1]), .sel(S));
  Multiplexer #(.disabled(0), .enable("false")) multiplexer_3 (.in0(A[1]), .in1(A[3]), .out(F[2]), .sel(S));
  Multiplexer #(.disabled(0), .enable("false")) multiplexer_4 (.in0(A[2]), .in1(RSerial_input_R), .out(F[3]), .sel(S));
endmodule

module AU (
  input  cin,
  input  [3:0] A,
  input  [3:0] B,
  input  _0,
  input  [1:0] s,
  output [3:0] Y,
  output cout
);

  wire _1_out, adder_1_cout, adder_2_cout, adder_3_cout, multiplexer_1_out, multiplexer_2_out,
       multiplexer_3_out, multiplexer_4_out, not_1_out, not_2_out, not_3_out, not_4_out;

  not _1 (_1_out, _0);
  not not_1 (not_1_out, B[0]);
  not not_2 (not_2_out, B[1]);
  not not_3 (not_3_out, B[2]);
  not not_4 (not_4_out, B[3]);
  Multiplexer #(.select(2), .disabled(0), .enable("false")) multiplexer_1 (
    .in0(B[0]), .in1(not_1_out), .in2(_0), .in3(_1_out), .out(multiplexer_1_out), .sel(s));
  Multiplexer #(.select(2), .disabled(0), .enable("false")) multiplexer_2 (
    .in0(B[1]), .in1(not_2_out), .in2(_0), .in3(_1_out), .out(multiplexer_2_out), .sel(s));
  Multiplexer #(.select(2), .disabled(0), .enable("false")) multiplexer_3 (
    .in0(B[2]), .in1(not_3_out), .in2(_0), .in3(_1_out), .out(multiplexer_3_out), .sel(s));
  Multiplexer #(.select(2), .disabled(0), .enable("false")) multiplexer_4 (
    .in0(B[3]), .in1(not_4_out), .in2(_0), .in3(_1_out), .out(multiplexer_4_out), .sel(s));
  Adder #(.width(1)) adder_1 (.a(A[0]), .b(multiplexer_1_out), .out(Y[0]), .cin(cin), .cout(adder_1_cout));
  Adder #(.width(1)) adder_2 (.a(A[1]), .b(multiplexer_2_out), .out(Y[1]), .cin(adder_1_cout), .cout(adder_2_cout));
  Adder #(.width(1)) adder_3 (.a(A[2]), .b(multiplexer_3_out), .out(Y[2]), .cin(adder_2_cout), .cout(adder_3_cout));
  Adder #(.width(1)) adder_4 (.a(A[3]), .b(multiplexer_4_out), .out(Y[3]), .cin(adder_3_cout), .cout(cout));
endmodule
